# Fritzing sketch 28BYJ-48_connection_example (saved by Fritzing 0.9.3b)
breadboards: 1

parts:
  M1 = DOIT Esp32 DevKit v1 (30 pins long, 11 pins width) [part_number=ESP32S-PIN30]
  X2 = X113647 Stepper Driver Board [part_number=X113647 package=board]
  MOTOR3 = 28BYJ-48 Stepper Motor
  Power_plug1 = Power plug

nets:
  GND: M1.GND, X2.GND, Power_plug1.GND
  N1: M1.D19, X2.IN4
  N2: M1.D21, X2.IN3
  N3: M1.D22, X2.IN2
  N4: M1.D23, X2.IN1
  N5: X2.+V, Power_plug1.VCC
  N6: X2.BLUE, MOTOR3.BLUE
  N7: X2.PINK, MOTOR3.PINK
  N8: X2.YELLOW, MOTOR3.YELLOW
  N9: X2.ORANGE, MOTOR3.ORANGE
  N10: X2.RED, MOTOR3.RED

notes:
  HexVitor
  (GitHub)
  Project: 28BYJ-48 module
  Author: Vítor Carvalho
  Date: Dec 29, 2019
  License: MIT
  28BYJ-48
  ULN2003
  IN1 IN2 IN3 IN4 GND VCC
  23 22 21 19 GND VCC
  5V ~ 12V

custom parts:
  DOIT Esp32 DevKit v1 (30 pins long, 11 pins width): The DOIT Esp32 DevKit v1 is one of the development board created by DOIT to evaluate the ESP-WROOM-32 module. It is based on the ESP32 microcontroller that boasts Wifi, Bluetooth, Ethernet and Low Power support all in a single chip. (vanepp) made breadboard work, adjusted pin numbering and labels and reduced size of schematic and cleaned up pcb. This chip is 30pins long (2 x15) and 11 pins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
  X113647 Stepper Driver Board: A common stepper motor driver board based on ULN2003APG darlington array
  28BYJ-48 Stepper Motor: 28BYJ-48 gear-reduction stepper motor (small)
