# Fritzing sketch LCD_connection_example (saved by Fritzing 0.9.3b)
breadboards: 1

parts:
  M1 = DOIT Esp32 DevKit v1 (30 pins long, 11 pins width) [part_number=ESP32S-PIN30]
  LCD1 = LCD screen
  U1 = POT [package=pot_mammoth]

nets:
  GND: M1.GND, LCD1.VSS, LCD1.R/W, LCD1.LED-, U1.E
  N1: M1.D25, LCD1.DB7
  N2: M1.D26, LCD1.DB6
  N3: M1.D27, LCD1.DB5
  N4: M1.D14, LCD1.DB4
  N5: M1.D12, LCD1.E
  N6: M1.D13, LCD1.RS
  VIN: M1.VIN, LCD1.VDD, LCD1.LED+, U1.S
  N7: LCD1.V0, U1.A

notes:
  1K / 10K POT
  VS VD V0 RS RW E D0 D1 D2 D3 D4 D5 D6 D7 A K
  - + Pot 13 - 12 - - - - 14 27 26 25 + -
  5V from VIN and GND
  pins (internally connected to the ESP32 voltage regulator input)
  Project: LCD Module
  Author: Vítor Carvalho
  Date: Dec 26, 2019
  License: MIT
  HexVitor
  (GitHub)

custom parts:
  DOIT Esp32 DevKit v1 (30 pins long, 11 pins width): The DOIT Esp32 DevKit v1 is one of the development board created by DOIT to evaluate the ESP-WROOM-32 module. It is based on the ESP32 microcontroller that boasts Wifi, Bluetooth, Ethernet and Low Power support all in a single chip. (vanepp) made breadboard work, adjusted pin numbering and labels and reduced size of schematic and cleaned up pcb. This chip is 30pins long (2 x15) and 11 pins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
