# Fritzing sketch LCD_I2C_connection_example (saved by Fritzing 0.9.3b)
breadboards: 1

parts:
  Componente1 = LCD1602-I2C
  M1 = DOIT Esp32 DevKit v1 (30 pins long, 11 pins width) [part_number=ESP32S-PIN30]

nets:
  GND: Componente1.GND, M1.GND
  VCC: Componente1.VCC, M1.VIN
  N1: Componente1.SDA, M1.D19
  N2: Componente1.SCL, M1.D18

notes:
  5V from VIN and GND pins (internally connected to the ESP32 voltage regulator input)
  HexVitor (GitHub)
  Project: LCD Module (I2C)
  Author: Vítor Carvalho
  Date: Dec 27, 2019
  License: MIT
  GND VCC SDA SCL
  GND 5V 19 18

custom parts:
  LCD1602-I2C: A standard character display, usually with 2x16 characters. Comes in many colors with LCM1602 IIC attached.
  DOIT Esp32 DevKit v1 (30 pins long, 11 pins width): The DOIT Esp32 DevKit v1 is one of the development board created by DOIT to evaluate the ESP-WROOM-32 module. It is based on the ESP32 microcontroller that boasts Wifi, Bluetooth, Ethernet and Low Power support all in a single chip. (vanepp) made breadboard work, adjusted pin numbering and labels and reduced size of schematic and cleaned up pcb. This chip is 30pins long (2 x15) and 11 pins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
