# Fritzing sketch Ultrasonic_connection_example (saved by Fritzing 0.9.3b)
breadboards: 1

parts:
  M1 = DOIT Esp32 DevKit v1 (30 pins long, 11 pins width) [part_number=ESP32S-PIN30]
  hc-sr1 = hc-sr04

nets:
  GND: M1.GND, hc-sr1.GND
  N1: M1.D19, hc-sr1.Echo
  N2: M1.D21, hc-sr1.Trig
  VIN: M1.VIN, hc-sr1.VCC

notes:
  HexVitor
  (GitHub)
  Project: Ultrasonic module
  Author: Vítor Carvalho
  Date: Jan 01, 2020
  License: MIT
  VCC Trig Echo GND
  VIN 21 19 GND
  HC-SR04

custom parts:
  DOIT Esp32 DevKit v1 (30 pins long, 11 pins width): The DOIT Esp32 DevKit v1 is one of the development board created by DOIT to evaluate the ESP-WROOM-32 module. It is based on the ESP32 microcontroller that boasts Wifi, Bluetooth, Ethernet and Low Power support all in a single chip. (vanepp) made breadboard work, adjusted pin numbering and labels and reduced size of schematic and cleaned up pcb. This chip is 30pins long (2 x15) and 11 pins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
